# Fritzing sketch musicbox (saved by Fritzing 0.9.3b)

parts:
  MCU1 = Raspberry Pi Zero
  Part1 = RFID-RC522-v3
  S1 = Square Pushbutton
  R1 = Resistor [tolerance=±5% resistance=1k package="0805 [SMD]"]
  LED1 = smd LED [color="Red (633nm)" package="0603 [SMD]"]
  L6 = Inductor [package="1206 [SMD]"]
  C3 = Capacitor Polarized [package=panasonic_d]
  C4 = Capacitor Polarized [package=panasonic_d]

nets:
  N1: MCU1.pin_2, C3.+, C4.+
  N2: MCU1.pin_5, S1.leg1
  N3: MCU1.pin_6, MCU1.pin_9, MCU1.pin_14, MCU1.pin_20, MCU1.pin_30, Part1.GND, S1.leg0, LED1.cathode, L6.pin_0
  N4: MCU1.pin_8, R1.Pin_0
  N5: MCU1.pin_17, Part1.3.3V
  N6: MCU1.pin_18, Part1.IRQ
  N7: MCU1.pin_19, Part1.MOSI
  N8: MCU1.pin_21, Part1.MISO
  N9: MCU1.pin_22, Part1.RST
  N10: MCU1.pin_23, Part1.SCK
  N11: MCU1.pin_24, MCU1.pin_38, Part1.SDA
  N12: R1.Pin_1, LED1.anode
  N13: L6.pin_1, C3.-, C4.-

custom parts:
  RFID-RC522-v3: A simple China made RFID-RC522 Reader (6x4 cm); do check the pin labels, as this is a MFRC522 based clone.
